# Fritzing sketch alim (saved by Fritzing 0.7.7b)
breadboards: 1

parts:
  Power_plug1 = Power plug
  C1 = Electrolytic Capacitor [capacitance=4.2mF voltage=20V package="100 mil [THT, electrolytic]"]
  Q1 = PNP-Transistor [part_number="2N2905 / BC557B" package="TO92 [THT]"]
  LED1 = LED - 5mm [color="Red (633nm)" package="5 mm [THT]"]
  R7 = Resistor [tolerance=±5% resistance=1k package=THT]
  R4 = Resistor [tolerance=±5% resistance=6.8k package=THT]
  R2 = Resistor [tolerance=±5% resistance=12 power=1.5W package=THT]
  R2' = Resistor [tolerance=±5% resistance=12 package=THT]
  R3 = Resistor [tolerance=±5% resistance=2.2k package=THT]
  R5 = Resistor [tolerance=±5% resistance=2.2k package=THT]
  R6 = Resistor [tolerance=±5% resistance=22k package=THT]
  Q3 = NPN-Transistor [part_number="2N2222 / BC337" package="TO92 [THT]"]
  U1 = Voltage Regulator - Variable [package="TO220 [THT]"]
  C2 = Electrolytic Capacitor [capacitance=22µF package="100 mil [THT, electrolytic]"]
  D1 = Rectifier Diode [part_number=1N4007 package="300 mil [THT]"]
  D2 = Rectifier Diode [part_number=1N4007 package="300 mil [THT]"]
  R1 = Resistor [tolerance=±5% resistance=150 package=THT]
  RV1 = Rotary Potentiometer (Small) [maximum_resistance=2.2kΩ]
  LED2 = LED - 5mm [color="Green (570nm)" package="5 mm [THT]"]
  C3 = Electrolytic Capacitor [capacitance=10µF package="100 mil [THT, electrolytic]"]
  Power_plug2 = Power plug
  D3 = Rectifier Diode [part_number=1N4001 package="300 mil [THT]"]
  S1 = Toggle Switch [package=THT]
  R8 = Resistor [tolerance=±5% resistance=220 package=THT]
  RV6 = Rotary Potentiometer (Small) [maximum_resistance=1kΩ]
  S2 = Toggle Switch [package=THT]

nets:
  GND: Power_plug1.GND, C1.-, R7.Pin_1, R4.Pin_1, R6.Pin_1, Q3.E, C2.-, RV1.leg2, LED2.cathode, C3.-, Power_plug2.GND
  N1: Power_plug1.VCC, S1.COM
  N2: C1.+, Q1.E, R2.Pin_1, R2'.Pin_1, D3.cathode, RV6.leg1
  N3: Q1.B, R3.Pin_1
  N4: Q1.C, LED1.anode, R4.Pin_0, R5.Pin_1
  N5: LED1.cathode, R7.Pin_0
  N6: R2.Pin_0, R2'.Pin_0, U1.IN, D1.cathode, RV6.leg2
  N7: R3.Pin_0, RV6.wiper
  N8: R5.Pin_0, R6.Pin_0, Q3.B
  N9: Q3.C, U1.ADJ, C2.+, D2.anode, R1.Pin_1, RV1.leg1, RV1.wiper
  N10: U1.OUT, D1.anode, D2.cathode, R1.Pin_0, S2.COM
  N11: LED2.anode, R8.Pin_1
  N12: C3.+, Power_plug2.VCC, R8.Pin_0, S2.L2
  N13: D3.anode, S1.L2
